// Logisim project sistemasdigitais.circ as structural Verilog: 1 circuit, main circuit main
module main (
  input  a,
  input  b,
  input  c,
  input  d
);

  wire a_prime_b_out, a_prime_out, ab_prime_d_prime_out, b_out, b_prime_c_out, b_prime_cd_prime_out,
       b_prime_d_out, bc_prime_out, c_out, c_prime_d_out, c_prime_d_prime_out, c_prime_out, cd_out, d_out,
       db_out, not_1_out, not_2_out, not_3_out, not_4_out, undriven, undriven_2, undriven_3, undriven_4,
       undriven_5, undriven_6, undriven_7, undriven_8, undriven_9, undriven_10, undriven_11, undriven_12,
       undriven_13, undriven_14, undriven_15, undriven_16, undriven_17, undriven_18, undriven_19,
       undriven_20, undriven_21, undriven_22, undriven_23, undriven_24, undriven_25, undriven_26,
       undriven_27, undriven_28, undriven_29, undriven_30, undriven_31, undriven_32, undriven_33;

  not not_1 (not_1_out, a);
  not not_2 (not_2_out, b);
  not not_3 (not_3_out, d);
  not not_4 (not_4_out, c);
  and ab_prime_d_prime (ab_prime_d_prime_out, a, not_2_out, not_3_out, undriven_6);
  and db (db_out, d, b, undriven_16, undriven_25);
  and a_prime_b (a_prime_b_out, not_1_out, b, undriven_7, undriven_26);
  and c_prime_d_prime (c_prime_d_prime_out, not_4_out, not_3_out, undriven_17, undriven_27);
  and cd (cd_out, c, d, undriven_18, undriven_8);
  and c_prime_d (c_prime_d_out, not_4_out, d, undriven_19, undriven_28);
  and bc_prime (bc_prime_out, b, not_4_out, undriven_9, undriven_29);
  and b_prime_cd_prime (b_prime_cd_prime_out, not_2_out, c, not_3_out, undriven_30);
  and b_prime_c (b_prime_c_out, not_2_out, c, undriven_20, undriven_10);
  and b_prime_d (b_prime_d_out, not_2_out, d, undriven_21, undriven_11);
  and a_prime (a_prime_out, not_1_out, undriven_31, undriven_12, undriven);
  and c_prime (c_prime_out, not_4_out, undriven_32, undriven_2, undriven_3);
  and u_b (b_out, b, undriven_13, undriven_4, undriven_14);
  and u_c (c_out, c, undriven_22, undriven_33, undriven_23);
  and u_d (d_out, undriven_24, undriven_15, undriven_5, d);
  // AND_Gate and_1 is placed but not wired
  // OR_Gate or_1 has open pins: in0=c_out, out=open
  // OR_Gate or_2 has open pins: in0=c_prime_out, in1=ab_prime_d_prime_out, in2=db_out, in3=a_prime_b_out, out=open
  // OR_Gate or_3 is placed but not wired
  // OR_Gate or_4 is placed but not wired
  // OR_Gate or_5 is placed but not wired
  // OR_Gate or_6 is placed but not wired
  // OR_Gate or_7 is placed but not wired
endmodule
